# Fritzing sketch programmer_un_attiny25v - copie (saved by Fritzing 0.9.1b)
breadboards: 1

parts:
  LED9 = LED - 5mm [color="Green (560nm)" package="5 mm [THT]"]
  LED10 = LED - 5mm [color="Red (633nm)" package="5 mm [THT]"]
  R7 = Resistor [tolerance=±5% resistance=220 package=THT]
  LED11 = LED - 5mm [color="Orange (612nm)" package="5 mm [THT]"]
  R8 = Resistor [tolerance=±5% resistance=220 package=THT]
  U2 = ATTINY45 [package=dip]
  LED12 = LED - 5mm [color="Green (560nm)" package="5 mm [THT]"]
  Composant3 = Arduino Uno (Rev3)
  R11 = Resistor [tolerance=±5% resistance=220 package=THT]
  R12 = Resistor [tolerance=±5% resistance=220 package=THT]

nets:
  N1: LED9.cathode, R11.Pin_1
  N2: LED9.anode, Composant3.D9_PWM
  N3: LED10.cathode, R8.Pin_1
  N4: LED10.anode, Composant3.D8
  GND: R7.Pin_0, R8.Pin_0, U2.GND, Composant3.GND, R11.Pin_0, R12.Pin_1
  N5: R7.Pin_1, LED11.cathode
  N6: LED11.anode, Composant3.D7
  N7: U2.PB5(NRES), Composant3.D10_PWM/SS
  N8: U2.PB4(ADC2), LED12.anode
  N9: U2.PB0(MOSI), Composant3.D11_PWM/MOSI
  N10: U2.PB1(MISO), Composant3.D12/MISO
  N11: U2.PB2(SCK_ADC1), Composant3.D13/SCK
  VCC: U2.VCC, Composant3.5V
  N12: LED12.cathode, R12.Pin_0
